# Fritzing sketch scheme (saved by Fritzing 0.9.3b)

parts:
  Часть2 = Arduino Mega 2560 (Rev3)
  Часть3 = Arduino Ethernet Shield (Rev3)
  AM1 = AM2302 Humidity and Temperature Sensor
  Часть4 = Adafruit TSL2561 [part_number="Adafruit #439"]
  U1 = MLX90614 [package=to-39]

nets:
  N1: Часть2.D21/SCL, Часть4.SCL, U1.VSS
  N2: Часть2.D20/SDA, Часть4.SDA, U1.VDD
  N3: Часть3.D2, AM1.DATA
  3V3: Часть3.3V3, AM1.VDD, Часть4.3.3V, U1.PWM_SDA
  GND: Часть3.GND, AM1.GND, Часть4.GND, U1.SCL_VZ

notes:
  MLX90615
  Arduino MEGA
  DHT22(AM2302)
  Ethernet Shield
  GY-2561

custom parts:
  Adafruit TSL2561: The TSL2561 luminosity sensor is an advanced digital light sensor, ideal for use in a wide range of light situations. Compared to low cost CdS cells, this sensor is more precise, allowing for exact lux calculations and can be configured for different gain/timing ranges to detect light ranges from up to 0.1 - 40,000+ Lux on the fly. The best part of this sensor is that it contains both infrared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
